// Logisim project 16 BIT REGISTER.circ as structural Verilog: 1 circuit, main circuit main
module main (
  input  [15:0] in_1,
  input  CLK,
  input  INC,
  input  LD,
  input  CLR,
  output [15:0] out_6
);

  wire or_1_out;
  wire [15:0] adder_1_out, multiplexer_1_out;

  Adder #(.width(16)) adder_1 (.a(16'h1), .b(out_6), .out(adder_1_out));  // open: cin, cout
  Multiplexer #(.width(16)) multiplexer_1 (
    .in0(in_1), .in1(adder_1_out), .out(multiplexer_1_out), .sel(INC));  // open: en
  or or_1 (or_1_out, INC, LD);
  Register #(.width(16)) register_1 (.D(multiplexer_1_out), .en(or_1_out), .Q(out_6), .clk(CLK), .clr(CLR));
endmodule
