// Logisim project 7 BIT REGISTER.circ as structural Verilog: 1 circuit, main circuit main
module main (
  input  [6:0] in_1,
  input  LD,
  input  CLK,
  input  CLR,
  output [6:0] out_5
);

  Register #(.width(7)) register_1 (.D(in_1), .en(LD), .Q(out_5), .clk(CLK), .clr(CLR));
endmodule
