// Logisim project DECODEMICROLOGIC.circ as structural Verilog: 1 circuit, main circuit main
module main (
  input  [2:0] F1,
  input  [2:0] F2,
  input  [2:0] F3,
  output ADD,
  output CLRAC,
  output INC_AC,
  output LD_ACFDR,
  output LDARFDR,
  output LD_ARFPC,
  output WRITE,
  output SUB,
  output OR,
  output AND,
  output READ,
  output LD_DR_F_AR,
  output INC_DR,
  output LD_DR_F_PC,
  output XOR,
  output COM,
  output SHL,
  output SHR,
  output INC_PC,
  output LD_PC_F_AR,
  output RESERVED
);

  Decoder #(.select(3)) decoder_1 (
    .out1(ADD), .out2(CLRAC), .out3(INC_AC), .out4(LD_ACFDR), .out5(LDARFDR), .out6(LD_ARFPC), .out7(WRITE),
    .sel(F1));  // open: out0, en
  Decoder #(.select(3)) decoder_2 (
    .out1(SUB), .out2(OR), .out3(AND), .out4(READ), .out5(LD_DR_F_AR), .out6(INC_DR), .out7(LD_DR_F_PC),
    .sel(F2));  // open: out0, en
  Decoder #(.select(3)) decoder_3 (
    .out1(XOR), .out2(COM), .out3(SHL), .out4(SHR), .out5(INC_PC), .out6(LD_PC_F_AR), .out7(RESERVED),
    .sel(F3));  // open: out0, en
endmodule
