// Logisim project INPUT LOGIC.circ as structural Verilog: 1 circuit, main circuit main
module main (
  input  I1,
  input  I0,
  input  T,
  output S1,
  output S0,
  output LD
);

  wire and_1_out, and_2_out, not_1_out;

  not not_1 (not_1_out, I1);
  and and_1 (and_1_out, I1, I0);
  and and_2 (and_2_out, not_1_out, T);
  or or_1 (S0, and_1_out, and_2_out);
  and and_3 (LD, I0, not_1_out, T);

  assign S1 = I1;
endmodule
