// Logisim project RAM.circ as structural Verilog: 1 circuit, main circuit main
module main (
  input  [10:0] ADDRESS,
  input  [15:0] DATA,
  input  WRITE,
  input  READ,
  input  CLOCK,
  output [15:0] out_6
);

  RAM #(.addrWidth(11), .dataWidth(16), .bus("separate")) ram_1 (
    .addr(ADDRESS), .din(DATA), .data(out_6), .str(WRITE), .clk(CLOCK), .ld(READ));  // open: sel, clr
endmodule
