// Logisim project IncReg12.circ as structural Verilog: 1 circuit, main circuit main
module main (
  input  [11:0] INP,
  input  clock,
  input  Inc,
  input  Load,
  input  Clear,
  output [11:0] OUT
);

  wire multiplexer_2_out;
  wire [11:0] adder_1_out, multiplexer_1_out;

  Multiplexer #(.width(12)) multiplexer_1 (
    .in0(INP), .in1(adder_1_out), .out(multiplexer_1_out), .sel(Inc));  // open: en
  Adder #(.width(12)) adder_1 (.a(12'h1), .b(OUT), .out(adder_1_out));  // open: cin, cout
  Multiplexer multiplexer_2 (.in0(Load), .in1(Inc), .out(multiplexer_2_out), .sel(Inc));  // open: en
  Register #(.width(12)) register_1 (.D(multiplexer_1_out), .en(multiplexer_2_out), .Q(OUT), .clk(clock), .clr(Clear));
endmodule
