// Logisim project increamentREG.circ as structural Verilog: 1 circuit, main circuit main
module main (
  input  [15:0] INP,
  input  Clock,
  input  Inc,
  input  Load,
  input  Clear,
  output [15:0] OUT
);

  wire multiplexer_2_out;
  wire [15:0] adder_1_out, multiplexer_1_out;

  Multiplexer #(.width(16)) multiplexer_1 (
    .in0(INP), .in1(adder_1_out), .out(multiplexer_1_out), .sel(Inc));  // open: en
  Adder #(.width(16)) adder_1 (.a(16'h1), .b(OUT), .out(adder_1_out));  // open: cin, cout
  Multiplexer multiplexer_2 (.in0(Load), .in1(Inc), .out(multiplexer_2_out), .sel(Inc));  // open: en
  Register #(.width(16)) register_1 (.D(multiplexer_1_out), .en(multiplexer_2_out), .Q(OUT), .clk(Clock), .clr(Clear));
endmodule
